// Logisim project part1.circ as structural Verilog: 5 circuits, main circuit main
module main (
);

  wire adder_1_h, adder_1_i, adder_1_j, adder_1_k, adder_1_l, binaryaddition_1_a, binaryaddition_1_a_2,
       binaryaddition_1_b, binaryaddition_1_b_2, binaryaddition_1_c, binaryaddition_1_c_2,
       binaryaddition_1_d, binaryaddition_1_d_2, binaryaddition_1_e, binaryaddition_1_e_2,
       binaryaddition_1_f, binaryaddition_1_f_2, binaryaddition_1_g, binaryaddition_1_g_2, clock_1_out,
       clock_2_out, dec_counter_1__0, dec_counter_1__1, dec_counter_1__2, dec_counter_1__3, dec_counter_2__0,
       dec_counter_2__1, dec_counter_2__2, dec_counter_2__3, logicgates_1_a, logicgates_1_b, logicgates_1_c,
       logicgates_1_d, logicgates_1_e, logicgates_1_f, logicgates_1_g, logicgates_2_a, logicgates_2_b,
       logicgates_2_c, logicgates_2_d, logicgates_2_e, logicgates_2_f, logicgates_2_g;

  dec_counter dec_counter_1 (
    .Clock(clock_2_out), ._3(dec_counter_1__3), ._2(dec_counter_1__2), ._1(dec_counter_1__1),
    ._0(dec_counter_1__0));  // open: isNine
  Clock clock_1 (.out(clock_1_out));
  dec_counter dec_counter_2 (
    .Clock(clock_1_out), ._3(dec_counter_2__3), ._2(dec_counter_2__2), ._1(dec_counter_2__1),
    ._0(dec_counter_2__0));  // open: isNine
  Clock clock_2 (.out(clock_2_out));
  logicgates logicgates_1 (
    .W(dec_counter_2__3), .X(dec_counter_2__2), .Y(dec_counter_2__1), .Z(dec_counter_2__0),
    .g(logicgates_1_g), .d(logicgates_1_d), .a(logicgates_1_a), .b(logicgates_1_b), .f(logicgates_1_f),
    .e(logicgates_1_e), .c(logicgates_1_c));
  adder adder_1 (
    .D(dec_counter_2__0), .Z(dec_counter_1__0), .C(dec_counter_2__1), .Y(dec_counter_1__1),
    .B(dec_counter_2__2), .X(dec_counter_1__2), .A(dec_counter_2__3), .W(dec_counter_1__3), .L(adder_1_l),
    .K(adder_1_k), .J(adder_1_j), .I(adder_1_i), .H(adder_1_h));
  logicgates logicgates_2 (
    .W(dec_counter_1__3), .X(dec_counter_1__2), .Y(dec_counter_1__1), .Z(dec_counter_1__0),
    .g(logicgates_2_g), .d(logicgates_2_d), .a(logicgates_2_a), .b(logicgates_2_b), .f(logicgates_2_f),
    .e(logicgates_2_e), .c(logicgates_2_c));
  _7_Segment_Display u_7_segment_display_1 (
    .g(logicgates_1_g), .f(logicgates_1_f), .a(logicgates_1_a), .b(logicgates_1_b), .e(logicgates_1_e),
    .d(logicgates_1_d), .c(logicgates_1_c));  // open: dp
  _7_Segment_Display u_7_segment_display_2 (
    .g(logicgates_2_g), .f(logicgates_2_f), .a(logicgates_2_a), .b(logicgates_2_b), .e(logicgates_2_e),
    .d(logicgates_2_d), .c(logicgates_2_c));  // open: dp
  binaryaddition binaryaddition_1 (
    ._1(adder_1_l), ._2(adder_1_k), ._4(adder_1_j), ._8(adder_1_i), ._16(adder_1_h), .a(binaryaddition_1_a),
    .b(binaryaddition_1_b), .c(binaryaddition_1_c), .d(binaryaddition_1_d), .e(binaryaddition_1_e),
    .f(binaryaddition_1_f), .g(binaryaddition_1_g), .a_2(binaryaddition_1_a_2), .b_2(binaryaddition_1_b_2),
    .c_2(binaryaddition_1_c_2), .d_2(binaryaddition_1_d_2), .e_2(binaryaddition_1_e_2),
    .f_2(binaryaddition_1_f_2), .g_2(binaryaddition_1_g_2));
  _7_Segment_Display u_7_segment_display_3 (
    .g(binaryaddition_1_g), .f(binaryaddition_1_f), .a(binaryaddition_1_a), .b(binaryaddition_1_b),
    .e(binaryaddition_1_e), .d(binaryaddition_1_d), .c(binaryaddition_1_c));  // open: dp
  _7_Segment_Display u_7_segment_display_4 (
    .g(binaryaddition_1_g_2), .f(binaryaddition_1_f_2), .a(binaryaddition_1_a_2), .b(binaryaddition_1_b_2),
    .e(binaryaddition_1_e_2), .d(binaryaddition_1_d_2), .c(binaryaddition_1_c_2));  // open: dp
endmodule

module dec_counter (
  input  Clock,
  output _3,
  output _2,
  output _1,
  output _0,
  output isNine
);

  wire and_1_out, and_2_out, and_3_out, and_4_out, and_5_out, and_6_out, and_7_out, D1_qn, D2_qn, D3_qn,
       D4_qn, or_1_out, or_2_out, or_3_out;

  and and_1 (and_1_out, _3, D4_qn);
  and and_2 (and_2_out, _1, _0, _2);
  and and_3 (and_3_out, _2, D3_qn);
  and and_4 (and_4_out, _2, D4_qn);
  and and_5 (and_5_out, _1, _0, D2_qn);
  and and_6 (and_6_out, _1, D4_qn);
  and and_7 (and_7_out, D3_qn, D1_qn, _0);
  or or_1 (or_1_out, and_1_out, and_2_out);
  or or_2 (or_2_out, and_3_out, and_4_out, and_5_out);
  or or_3 (or_3_out, and_6_out, and_7_out);
  D_Flip_Flop #(.trigger("falling")) D1 (.clk(Clock), .D(or_1_out), .Q(_3), .Qn(D1_qn));  // open: preset, en, reset
  D_Flip_Flop #(.trigger("falling")) D2 (.clk(Clock), .D(or_2_out), .Q(_2), .Qn(D2_qn));  // open: preset, en, reset
  D_Flip_Flop #(.trigger("falling")) D3 (.clk(Clock), .D(or_3_out), .Q(_1), .Qn(D3_qn));  // open: preset, en, reset
  D_Flip_Flop #(.trigger("falling")) D4 (.clk(Clock), .D(D4_qn), .Q(_0), .Qn(D4_qn));  // open: preset, en, reset
  and and_8 (isNine, _0, D3_qn, D2_qn, _3);
endmodule

module logicgates (
  input  W,
  input  X,
  input  Y,
  input  Z,
  output g,
  output d,
  output a,
  output b,
  output f,
  output e,
  output c
);

  wire and_1_out, and_2_out, and_3_out, and_4_out, and_5_out, and_6_out, and_7_out, and_8_out, and_9_out,
       and_10_out, not_1_out, not_3_out, not_4_out, xnor_1_out, xnor_2_out;

  not not_1 (not_1_out, Z);
  // NOT_Gate not_2 has open pins: in=W, out=open
  not not_3 (not_3_out, X);
  not not_4 (not_4_out, Y);
  and and_1 (and_1_out, not_1_out, Y);
  and and_2 (and_2_out, Y, not_3_out);
  and and_3 (and_3_out, X, not_4_out);
  and and_4 (and_4_out, not_3_out, Y);
  and and_5 (and_5_out, Y, not_1_out);
  and and_6 (and_6_out, not_4_out, Z, X);
  and and_7 (and_7_out, not_1_out, not_3_out);
  xnor xnor_1 (xnor_1_out, X, Z);
  xnor xnor_2 (xnor_2_out, Z, Y);
  and and_8 (and_8_out, not_1_out, not_4_out);
  and and_9 (and_9_out, not_3_out, not_1_out);
  and and_10 (and_10_out, Y, not_1_out);
  or or_1 (c, not_4_out, Z, X);
  or or_2 (g, W, and_1_out, and_2_out, and_3_out);
  or or_3 (d, and_4_out, and_5_out, and_6_out, and_7_out);
  or or_4 (a, xnor_1_out, Y, W);
  or or_5 (b, xnor_2_out, not_3_out);
  or or_6 (f, W, and_8_out, X);
  or or_7 (e, and_9_out, and_10_out);
endmodule

module adder (
  input  D,
  input  Z,
  input  C,
  input  Y,
  input  B,
  input  X,
  input  A,
  input  W,
  output L,
  output K,
  output J,
  output I,
  output H
);

  wire and_1_out, and_2_out, and_3_out, and_4_out, and_5_out, and_6_out, and_7_out, or_1_out, or_2_out,
       xor_2_out, xor_3_out, xor_4_out;

  xor xor_1 (L, D, Z);
  and and_1 (and_1_out, D, Z);
  xor xor_2 (xor_2_out, C, Y);
  and and_2 (and_2_out, C, Y);
  xor xor_3 (xor_3_out, B, X);
  and and_3 (and_3_out, B, X);
  xor xor_4 (xor_4_out, A, W);
  and and_4 (and_4_out, A, W);
  xor xor_5 (K, and_1_out, xor_2_out);
  xor xor_6 (J, or_1_out, xor_3_out);
  xor xor_7 (I, or_2_out, xor_4_out);
  and and_5 (and_5_out, xor_2_out, and_1_out);
  and and_6 (and_6_out, or_1_out, xor_3_out);
  and and_7 (and_7_out, or_2_out, xor_4_out);
  or or_1 (or_1_out, and_5_out, and_2_out);
  or or_2 (or_2_out, and_6_out, and_3_out);
  or or_3 (H, and_7_out, and_4_out);
endmodule

module binaryaddition (
  input  _1,
  input  _2,
  input  _4,
  input  _8,
  input  _16,
  output a,
  output b,
  output c,
  output d,
  output e,
  output f,
  output g,
  output a_2,
  output b_2,
  output c_2,
  output d_2,
  output e_2,
  output f_2,
  output g_2
);

  wire _0_2_out, _0_3_out, _0_out, _1_2_out, _1_3_out, _1_out, _2_2_out, _2_out, _3_2_out, _3_out, _4_2_out,
       _4_out, _5_2_out, _5_out, _6_2_out, _6_out, _7_2_out, _7_out, _8_2_out, _8_out, _9_2_out, _9_out,
       _10_out, _11_out, _12_out, _13_out, _14_out, _15_out, _16_out, _17_out, _18_out, and_1_out, not_1_out,
       not_2_out, not_3_out, not_4_out, not_5_out, not_6_out, not_7_out;

  not not_1 (not_1_out, _1);
  not not_2 (not_2_out, _2);
  not not_3 (not_3_out, _4);
  not not_4 (not_4_out, _8);
  not not_5 (not_5_out, _16);
  and u__8 (_8_out, not_1_out, not_2_out, not_3_out, _8, not_5_out);
  and _9 (_9_out, not_5_out, _8, not_3_out, not_2_out, _1);
  and _10 (_10_out, not_1_out, _2, not_3_out, _8, not_5_out);
  and _11 (_11_out, _1, _2, not_3_out, _8, not_5_out);
  and _12 (_12_out, not_5_out, _8, _4, not_2_out, not_1_out);
  and _13 (_13_out, _1, not_2_out, _4, _8, not_5_out);
  and _14 (_14_out, not_1_out, _2, _4, _8, not_5_out);
  and _15 (_15_out, _1, _2, _4, _8, not_5_out);
  and u__16 (_16_out, not_1_out, not_2_out, not_3_out, not_4_out, _16);
  and u__1 (_1_out, _1, not_2_out, not_3_out, not_4_out, not_5_out);
  and u__2 (_2_out, not_1_out, _2, not_3_out, not_4_out, not_5_out);
  and _3 (_3_out, _1, _2, not_3_out, not_4_out, not_5_out);
  and u__4 (_4_out, not_1_out, not_2_out, _4, not_4_out, not_5_out);
  and _5 (_5_out, _1, not_2_out, _4, not_4_out, not_5_out);
  and _6 (_6_out, not_1_out, _2, _4, not_4_out, not_5_out);
  and _7 (_7_out, _1, _2, _4, not_4_out, not_5_out);
  and _0 (_0_out, not_5_out, not_4_out, not_3_out, not_2_out, not_1_out);
  and _17 (_17_out, _16, not_4_out, not_3_out, not_2_out, _1);
  and _18 (_18_out, _16, not_4_out, not_3_out, not_1_out, _2);
  or _1_2 (_1_2_out, _10_out, _11_out, _12_out, _13_out, _14_out, _15_out, _16_out, _17_out, _18_out);
  not not_6 (not_6_out, _1_2_out);
  or _0_2 (_0_2_out, _9_out, _8_out, _1_out, _2_out, _3_out, _4_out, _5_out, _6_out, _7_out, _0_out);
  not not_7 (not_7_out, _0_2_out);
  and and_1 (and_1_out, not_7_out, not_6_out);
  or _0_3 (_0_3_out, _0_out, _10_out);
  or _1_3 (_1_3_out, _1_out, _11_out);
  or _2_2 (_2_2_out, _2_out, _12_out);
  or _3_2 (_3_2_out, _3_out, _13_out);
  or _4_2 (_4_2_out, _4_out, _14_out);
  or _5_2 (_5_2_out, _5_out, _15_out);
  or _6_2 (_6_2_out, _16_out, _6_out);
  or _7_2 (_7_2_out, _7_out, _17_out);
  or _8_2 (_8_2_out, _8_out, _18_out);
  buf _9_2 (_9_2_out, _9_out);  // OR_Gate
  buf or_1 (a, _0_2_out);  // OR_Gate
  or or_2 (b, _1_2_out, _0_2_out);
  or or_3 (c, _1_2_out, _0_2_out);
  buf or_4 (d, _0_2_out);  // OR_Gate
  buf or_5 (e, _0_2_out);  // OR_Gate
  buf or_6 (f, _0_2_out);  // OR_Gate
  buf or_7 (g, and_1_out);  // OR_Gate
  or or_8 (a_2, _3_2_out, _5_2_out, _6_2_out, _7_2_out, _0_3_out, _9_2_out, _2_2_out, _8_2_out);
  or or_9 (b_2, _0_3_out, _8_2_out, _2_2_out, _1_3_out, _9_2_out, _7_2_out, _4_2_out, _3_2_out);
  or or_10 (c_2, _0_3_out, _8_2_out, _1_3_out, _9_2_out, _7_2_out, _6_2_out, _3_2_out, _4_2_out, _5_2_out);
  or or_11 (d_2, _0_3_out, _8_2_out, _2_2_out, _9_2_out, _6_2_out, _5_2_out, _3_2_out);
  or or_12 (e_2, _0_3_out, _8_2_out, _2_2_out, _6_2_out);
  or or_13 (f_2, _0_3_out, _8_2_out, _7_2_out, _9_2_out, _6_2_out, _8_2_out, _5_2_out, _4_2_out);
  or or_14 (g_2, _8_2_out, _2_2_out, _9_2_out, _6_2_out, _5_2_out, _4_2_out, _3_2_out);

  // Notes on the sheet:
  //   Either 0 or 1
  //   1 = b and c active
endmodule
